// Logisim project 4 bit binary up and down counter.circ as structural Verilog: 1 circuit, main circuit main
module main (
  input  Up,
  input  Down,
  output out_3,
  output out_4,
  output out_5,
  output out_6
);

  wire and_1_out, and_2_out, and_3_out, and_4_out, and_5_out, and_6_out, clock_1_out, j_k_ff_1_qn,
       j_k_ff_2_qn, j_k_ff_3_qn, or_1_out, or_2_out, or_3_out, or_4_out;

  and and_1 (and_1_out, Down, j_k_ff_1_qn);
  and and_2 (and_2_out, Up, out_6);
  and and_3 (and_3_out, and_1_out, j_k_ff_2_qn);
  and and_4 (and_4_out, and_2_out, out_5);
  and and_5 (and_5_out, and_4_out, out_4);
  and and_6 (and_6_out, and_3_out, j_k_ff_3_qn);
  or or_1 (or_1_out, Down, Up);
  or or_2 (or_2_out, and_1_out, and_2_out);
  or or_3 (or_3_out, and_3_out, and_4_out);
  or or_4 (or_4_out, and_6_out, and_5_out);
  Clock clock_1 (.out(clock_1_out));
  J_K_Flip_Flop j_k_ff_1 (
    .J(or_1_out), .clk(clock_1_out), .K(or_1_out), .Q(out_6), .Qn(j_k_ff_1_qn));  // open: preset, en, reset
  J_K_Flip_Flop j_k_ff_2 (
    .J(or_2_out), .clk(clock_1_out), .K(or_2_out), .Q(out_5), .Qn(j_k_ff_2_qn));  // open: preset, en, reset
  J_K_Flip_Flop j_k_ff_3 (
    .J(or_3_out), .clk(clock_1_out), .K(or_3_out), .Q(out_4), .Qn(j_k_ff_3_qn));  // open: preset, en, reset
  J_K_Flip_Flop j_k_ff_4 (.J(or_4_out), .clk(clock_1_out), .K(or_4_out), .Q(out_3));  // open: Qn, preset, en, reset
endmodule
