// Logisim project 4- bit binary counter with parralel load.circ as structural Verilog: 1 circuit, main circuit main
module main (
  input  Load,
  input  Count,
  input  I0,
  input  I1,
  input  I2,
  input  I3,
  output out_7,
  output out_8,
  output out_9,
  output out_10
);

  wire and_1_out, and_2_out, and_3_out, and_4_out, and_5_out, and_6_out, and_7_out, and_8_out, and_9_out,
       and_10_out, and_11_out, and_12_out, clock_1_out, not_1_out, not_2_out, not_3_out, not_4_out,
       not_5_out, or_1_out, or_2_out, or_3_out, or_4_out, or_5_out, or_6_out, or_7_out, or_8_out;

  not not_1 (not_1_out, Load);
  not not_2 (not_2_out, I0);
  not not_3 (not_3_out, I1);
  not not_4 (not_4_out, I2);
  not not_5 (not_5_out, I3);
  and and_1 (and_1_out, Count, not_1_out);
  and and_2 (and_2_out, I0, Load);
  and and_3 (and_3_out, Load, not_2_out);
  and and_4 (and_4_out, I1, Load);
  and and_5 (and_5_out, Load, not_3_out);
  and and_6 (and_6_out, I2, Load);
  and and_7 (and_7_out, Load, not_4_out);
  and and_8 (and_8_out, I3, Load);
  and and_9 (and_9_out, Load, not_5_out);
  and and_10 (and_10_out, and_1_out, out_10);
  and and_11 (and_11_out, and_10_out, out_9);
  and and_12 (and_12_out, and_11_out, out_8);
  or or_1 (or_1_out, and_1_out, and_2_out);
  or or_2 (or_2_out, and_1_out, and_3_out);
  or or_3 (or_3_out, and_4_out, and_10_out);
  or or_4 (or_4_out, and_10_out, and_5_out);
  or or_5 (or_5_out, and_6_out, and_11_out);
  or or_6 (or_6_out, and_11_out, and_7_out);
  or or_7 (or_7_out, and_8_out, and_12_out);
  or or_8 (or_8_out, and_12_out, and_9_out);
  Clock clock_1 (.out(clock_1_out));
  J_K_Flip_Flop j_k_ff_1 (.J(or_1_out), .clk(clock_1_out), .K(or_2_out), .Q(out_10));  // open: Qn, preset, en, reset
  J_K_Flip_Flop j_k_ff_2 (.J(or_3_out), .clk(clock_1_out), .K(or_4_out), .Q(out_9));  // open: Qn, preset, en, reset
  J_K_Flip_Flop j_k_ff_3 (.J(or_5_out), .clk(clock_1_out), .K(or_6_out), .Q(out_8));  // open: Qn, preset, en, reset
  J_K_Flip_Flop j_k_ff_4 (.J(or_7_out), .clk(clock_1_out), .K(or_8_out), .Q(out_7));  // open: Qn, preset, en, reset
endmodule
