// Logisim project DE_Project.circ as structural Verilog: 1 circuit, main circuit main
module main (
  input  A1,
  input  A2,
  input  A4,
  input  A8
);

  wire A_out, and_1_out, and_2_out, and_3_out, and_4_out, and_5_out, and_6_out, and_7_out, and_8_out,
       and_9_out, and_10_out, and_11_out, and_12_out, and_13_out, B_out, C_out, D_out, G_out, not_1_out,
       not_2_out, not_3_out, not_4_out, not_5_out, not_6_out;

  not not_1 (not_1_out, A4);
  not not_2 (not_2_out, A8);
  not not_3 (not_3_out, A2);
  not not_4 (not_4_out, A2);
  not not_5 (not_5_out, A1);
  not not_6 (not_6_out, A8);
  and and_1 (and_1_out, not_1_out, not_2_out);
  and and_2 (and_2_out, not_2_out, A1);
  and and_3 (and_3_out, A4, not_3_out, A1);
  and and_4 (and_4_out, not_1_out, A1, A2);
  and and_5 (and_5_out, not_5_out, not_4_out);
  and and_6 (and_6_out, not_5_out, A8);
  and and_7 (and_7_out, not_5_out, A4);
  and and_8 (and_8_out, A2, A4, A8);
  and and_9 (and_9_out, not_1_out, not_4_out, A8);
  and and_10 (and_10_out, not_6_out, not_1_out, A2);
  and and_11 (and_11_out, not_6_out, A4, A1);
  and and_12 (and_12_out, A4, A1, not_4_out);
  and and_13 (and_13_out, A1, A2, not_1_out);
  or A (A_out, not_5_out, A2, A4, A8);
  or B (B_out, and_1_out, and_2_out, and_3_out, and_4_out);
  and C (C_out, not_2_out, not_4_out, not_1_out);
  or D (D_out, and_5_out, and_6_out, and_7_out, and_8_out, and_9_out);
  or G (G_out, and_10_out, and_11_out, and_12_out, and_13_out);
  _7_Segment_Display u_7_segment_display_1 (
    .g(G_out), .f(A_out), .a(A_out), .b(B_out), .e(A_out), .d(D_out), .c(C_out));  // open: dp

  // Notes on the sheet:
  //   E
  //   F
endmodule
