// Logisim project Incomplete Serial Substractor.circ as structural Verilog: 1 circuit, main circuit main
module main (
  input  Shift_Enable,
  input  Serial_Input,
  output out_3
);

  wire adder_1_out, button_1_out, d_ff_1_q, d_ff_2_q, multiplexer_1_out, not_1_out, not_2_out,
       shift_register_1_out, shift_register_2_out;

  Button button_1 (.out(button_1_out));
  Shift_Register #(.length(4)) shift_register_1 (
    .shift(Shift_Enable), .in(adder_1_out), .clk(button_1_out), .out(shift_register_1_out));  // open: load, clr, d0, q0, d1, q1, d2, q2, d3, q3
  Shift_Register #(.length(4)) shift_register_2 (
    .shift(Shift_Enable), .in(Serial_Input), .clk(button_1_out), .out(shift_register_2_out));  // open: load, clr, d0, q0, d1, q1, d2, q2, d3, q3
  not not_1 (not_1_out, shift_register_2_out);
  not not_2 (not_2_out, button_1_out);
  Multiplexer #(.enable("false")) multiplexer_1 (
    .in0(Shift_Enable), .in1(d_ff_2_q), .out(multiplexer_1_out), .sel(d_ff_1_q));
  Adder #(.width(1)) adder_1 (
    .a(shift_register_1_out), .b(not_1_out), .out(adder_1_out), .cin(multiplexer_1_out), .cout(out_3));
  D_Flip_Flop d_ff_1 (.clk(not_2_out), .D(Shift_Enable), .Q(d_ff_1_q));  // open: Qn, preset, en, reset
  D_Flip_Flop d_ff_2 (.clk(not_2_out), .D(out_3), .Q(d_ff_2_q));  // open: Qn, preset, en, reset
  Shift_Register #(.length(4)) shift_register_3 (
    .shift(Shift_Enable), .in(adder_1_out), .clk(button_1_out));  // open: out, load, clr, d0, q0, d1, q1, d2, q2, d3, q3

  // Notes on the sheet:
  //   Clock
  //   Ans
endmodule
