// Logisim project Pract10(Bidirectional Shift Register with Parallel Load).circ as structural Verilog: 1 circuit, main circuit main
module main (
  input  in_1,
  input  in_2,
  input  Serial_Input,
  input  Serial_Input_2,
  input  I3,
  input  I2,
  input  I1,
  input  I0,
  output A8,
  output A4,
  output A2,
  output A1
);

  wire clock_1_out, multiplexer_1_out, multiplexer_2_out, multiplexer_3_out, multiplexer_4_out;

  Clock clock_1 (.out(clock_1_out));
  Multiplexer #(.select(2)) multiplexer_1 (
    .in0(A8), .in1(Serial_Input), .in2(A4), .in3(I3), .out(multiplexer_1_out), .sel({in_2, in_1}));  // open: en
  D_Flip_Flop d_ff_1 (.clk(clock_1_out), .D(multiplexer_1_out), .Q(A8));  // open: Qn, preset, en, reset
  Multiplexer #(.select(2)) multiplexer_2 (
    .in0(A4), .in1(A8), .in2(A2), .in3(I2), .out(multiplexer_2_out), .sel({in_2, in_1}));  // open: en
  D_Flip_Flop d_ff_2 (.clk(clock_1_out), .D(multiplexer_2_out), .Q(A4));  // open: Qn, preset, en, reset
  Multiplexer #(.select(2)) multiplexer_3 (
    .in0(A2), .in1(A4), .in2(A1), .in3(I1), .out(multiplexer_3_out), .sel({in_2, in_1}));  // open: en
  D_Flip_Flop d_ff_3 (.clk(clock_1_out), .D(multiplexer_3_out), .Q(A2));  // open: Qn, preset, en, reset
  Multiplexer #(.select(2)) multiplexer_4 (
    .in0(A1), .in1(A2), .in2(Serial_Input_2), .in3(I0), .out(multiplexer_4_out), .sel({in_2, in_1}));  // open: en
  D_Flip_Flop d_ff_4 (.clk(clock_1_out), .D(multiplexer_4_out), .Q(A1));  // open: Qn, preset, en, reset

  // Notes on the sheet:
  //   (for Shift Right)
  //   (for Left Right)
endmodule
