// Logisim project Pract4(BCD to 84-2-1).circ as structural Verilog: 1 circuit, main circuit main
module main (
  input  B3,
  input  B2,
  input  B1,
  input  B0,
  output b3_2,
  output b2_2,
  output b1_2,
  output b0_2
);

  wire and_1_out, and_2_out, and_3_out, and_4_out, and_5_out, and_6_out, and_7_out, not_1_out, not_2_out,
       not_3_out, not_4_out;

  not not_1 (not_1_out, B3);
  not not_2 (not_2_out, B0);
  not not_3 (not_3_out, B1);
  not not_4 (not_4_out, B2);
  and and_1 (and_1_out, B1, not_2_out);
  and and_2 (and_2_out, not_3_out, B0);
  and and_3 (and_3_out, B1, not_4_out);
  and and_4 (and_4_out, B0, not_4_out);
  and and_5 (and_5_out, B2, not_3_out, not_2_out);
  and and_6 (and_6_out, B2, B0);
  and and_7 (and_7_out, B2, B1);
  or or_1 (b1_2, and_1_out, and_2_out);
  or or_2 (b3_2, and_6_out, and_7_out, B3);
  or or_3 (b2_2, and_3_out, and_4_out, and_5_out);

  assign b0_2 = B0;

  // Notes on the sheet:
  //   Weights
  //   8
  //   4
  //   -2
  //   -1
endmodule
