// Logisim project Pract4(Gray to Binary and BInary to Gray).circ as structural Verilog: 1 circuit, main circuit main
module main (
  input  g3,
  input  g2,
  input  g1,
  input  g0,
  output b3,
  output b2,
  output b1,
  output b0,
  output g3_2,
  output g2_2,
  output g1_2,
  output g0_2
);

  xor xor_1 (b2, g2, g3);
  xor xor_2 (b1, b2, g1);
  xor xor_3 (b0, b1, g0);
  xor xor_4 (g2_2, b2, g3);
  xor xor_5 (g1_2, b2, b1);
  xor xor_6 (g0_2, b1, b0);

  assign b3 = g3;
  assign g3_2 = g3;

  // Notes on the sheet:
  //   b2
  //   b1
  //   b0
  //   b3
endmodule
