// Logisim project Pract4(Square of a 3 bit number).circ as structural Verilog: 1 circuit, main circuit main
module main (
  input  A,
  input  B,
  input  C,
  input  in_4,
  output a0,
  output a1,
  output a2,
  output a3,
  output a4,
  output a5
);

  wire and_1_out, and_2_out, and_3_out, and_4_out, not_1_out, not_2_out, not_3_out;

  not not_1 (not_1_out, C);
  not not_2 (not_2_out, B);
  not not_3 (not_3_out, A);
  and and_1 (and_1_out, not_3_out, B, C);
  and and_2 (and_2_out, A, not_2_out, C);
  and and_3 (and_3_out, A, not_2_out);
  and and_4 (and_4_out, A, C);
  and and_5 (a5, A, B);
  and and_6 (a2, B, not_1_out);
  or or_1 (a3, and_1_out, and_2_out);
  or or_2 (a4, and_3_out, and_4_out);

  assign a0 = C;
  assign a1 = in_4;
endmodule
