// Logisim project Pract5(BCD Adder).circ as structural Verilog: 1 circuit, main circuit main
// 1
module main (
  input  in_1,
  input  Input_Carry,
  input  [3:0] nst_BCD_No,
  input  [3:0] in_4,
  output out_5,
  output [3:0] out_6
);

  wire adder_1_cout, and_1_out, and_2_out;
  wire [2:2] or_1_out;
  wire [3:0] adder_1_out;

  Adder #(.width(4)) adder_1 (.a(nst_BCD_No), .b(in_4), .out(adder_1_out), .cin(Input_Carry), .cout(adder_1_cout));
  and and_1 (and_1_out, adder_1_out[1], adder_1_out[3]);
  and and_2 (and_2_out, adder_1_out[3], adder_1_out[2]);
  or or_1 (or_1_out[2], and_1_out, and_2_out, adder_1_cout);
  Adder #(.width(4)) adder_2 (
    .a(adder_1_out), .b({in_1, {2{or_1_out[2]}}, in_1}), .out(out_6), .cout(out_5));  // open: cin

  // Notes on the sheet:
  //   2nd BCD No
endmodule
