// Logisim project Pract5(Excess-3 Adder).circ as structural Verilog: 1 circuit, main circuit main
module main (
  input  Input_Carry,
  input  in_2,
  input  [3:0] _1st_Excess_3_No,
  input  [3:0] in_4,
  input  in_5,
  output out_6,
  output [3:0] out_7
);

  wire [3:0] adder_1_out;
  wire [3:3] not_1_out;

  Adder #(.width(4)) adder_1 (.a(_1st_Excess_3_No), .b(in_4), .out(adder_1_out), .cin(Input_Carry), .cout(out_6));
  not not_1 (not_1_out[3], out_6);
  Adder #(.width(4)) adder_2 (
    .a(adder_1_out), .b({{2{not_1_out[3]}}, out_6, in_5}), .out(out_7), .cin(in_2));  // open: cout

  // Notes on the sheet:
  //   2nd Excess-3 No
  //   C
endmodule
