// Logisim project Pract6(Multiplexer).circ as structural Verilog: 1 circuit, main circuit east
module east (
  input  A,
  input  B,
  input  C,
  input  D,
  input  in_5,
  input  in_6,
  output F,
  output F_2,
  output F_3,
  output F_4
);

  wire not_1_out, not_2_out, not_3_out;

  not not_1 (not_1_out, A);
  not not_2 (not_2_out, C);
  not not_3 (not_3_out, D);
  Multiplexer #(.select(3)) multiplexer_1 (
    .in0(in_5), .in1(not_1_out), .in2(in_5), .in3(in_5), .in4(A), .in5(not_1_out), .in6(in_6), .in7(in_6),
    .out(F), .sel({B, C, D}));  // open: en
  Multiplexer #(.select(3)) multiplexer_2 (
    .in0(in_5), .in1(not_2_out), .in2(C), .in3(in_6), .in4(in_5), .in5(in_5), .in6(in_6), .in7(C), .out(F_2),
    .sel({A, B, D}));  // open: en
  Multiplexer #(.select(3)) multiplexer_3 (
    .in0(in_5), .in1(in_6), .in2(B), .in3(B), .in4(B), .in5(in_5), .in6(B), .in7(B), .out(F_3),
    .sel({A, C, D}));  // open: en
  Multiplexer #(.select(3)) multiplexer_4 (
    .in0(D), .in1(in_5), .in2(D), .in3(in_6), .in4(in_5), .in5(in_5), .in6(not_3_out), .in7(in_6), .out(F_4),
    .sel({A, B, C}));  // open: en
endmodule
