// Logisim project Pract8(Modulo-7 Synchronous Counter).circ as structural Verilog: 1 circuit, main circuit main
module main (
  input  in_1,
  output A,
  output B,
  output C
);

  wire and_1_out, clock_1_out, j_k_ff_2_qn, j_k_ff_3_qn, or_1_out, or_2_out;

  or or_1 (or_1_out, j_k_ff_3_qn, j_k_ff_2_qn);
  or or_2 (or_2_out, C, A);
  and and_1 (and_1_out, B, C);
  Clock clock_1 (.out(clock_1_out));
  J_K_Flip_Flop j_k_ff_1 (.J(or_1_out), .clk(clock_1_out), .K(in_1), .Q(C));  // open: Qn, preset, en, reset
  J_K_Flip_Flop j_k_ff_2 (.J(C), .clk(clock_1_out), .K(or_2_out), .Q(B), .Qn(j_k_ff_2_qn));  // open: preset, en, reset
  J_K_Flip_Flop j_k_ff_3 (.J(and_1_out), .clk(clock_1_out), .K(B), .Q(A), .Qn(j_k_ff_3_qn));  // open: preset, en, reset

  // Notes on the sheet:
  //   MODULO-7 SYNCHRONOUS COUNTER
  //   C
  //   B
  //   A
endmodule
