// Logisim project Pract9(Modulo 16 Ripple Counter).circ as structural Verilog: 1 circuit, main circuit main
module main (
  input  in_1,
  output A8,
  output A4,
  output A2,
  output A1
);

  wire clock_1_out, not_1_out, not_2_out, not_3_out;

  Clock clock_1 (.out(clock_1_out));
  T_Flip_Flop t_ff_1 (.clk(clock_1_out), .T(in_1), .Q(A1));  // open: Qn, preset, reset, en
  not not_1 (not_1_out, A1);
  T_Flip_Flop t_ff_2 (.clk(not_1_out), .T(in_1), .Q(A2));  // open: Qn, preset, reset, en
  not not_2 (not_2_out, A2);
  T_Flip_Flop t_ff_3 (.clk(not_2_out), .T(in_1), .Q(A4));  // open: Qn, preset, reset, en
  not not_3 (not_3_out, A4);
  T_Flip_Flop t_ff_4 (.clk(not_3_out), .T(in_1), .Q(A8));  // open: Qn, preset, reset, en
endmodule
