// Logisim project Pract9(Ripple Odd counter Modulo-16).circ as structural Verilog: 1 circuit, main circuit main
module main (
  input  in_1,
  input  in_2,
  input  in_3,
  input  in_4,
  output A8,
  output A4,
  output A2,
  output A1,
  output A8_2,
  output A4_2,
  output A2_2,
  output A1_2
);

  wire clock_1_out, clock_2_out, not_1_out, not_2_out, not_3_out, not_4_out, not_5_out;

  Clock clock_1 (.out(clock_1_out));
  not not_1 (not_1_out, A2_2);
  not not_2 (not_2_out, A4_2);
  T_Flip_Flop t_ff_1 (.clk(clock_1_out), .T(in_1), .Qn(A1_2));  // open: Q, preset, reset, en
  T_Flip_Flop t_ff_2 (.clk(clock_1_out), .T(in_3), .Q(A2_2));  // open: Qn, preset, reset, en
  T_Flip_Flop t_ff_3 (.clk(not_1_out), .T(in_3), .Q(A4_2));  // open: Qn, preset, reset, en
  T_Flip_Flop t_ff_4 (.clk(not_2_out), .T(in_3), .Q(A8_2));  // open: Qn, preset, reset, en
  Clock clock_2 (.out(clock_2_out));
  not not_3 (not_3_out, in_2);
  J_K_Flip_Flop j_k_ff_1 (.J(not_3_out), .clk(clock_2_out), .K(in_2), .Q(A1));  // open: Qn, preset, en, reset
  J_K_Flip_Flop j_k_ff_2 (.J(in_4), .clk(clock_2_out), .K(in_4), .Q(A2));  // open: Qn, preset, en, reset
  not not_4 (not_4_out, A2);
  J_K_Flip_Flop j_k_ff_3 (.J(in_4), .clk(not_4_out), .K(in_4), .Q(A4));  // open: Qn, preset, en, reset
  not not_5 (not_5_out, A4);
  J_K_Flip_Flop j_k_ff_4 (.J(in_4), .clk(not_5_out), .K(in_4), .Q(A8));  // open: Qn, preset, en, reset
endmodule
