// Logisim project Serial Adder.circ as structural Verilog: 1 circuit, main circuit main
module main (
  input  Shift_Enable,
  input  Serial_Input,
  output out_3
);

  wire adder_1_out, clock_1_out, d_ff_1_q, shift_register_1_out, shift_register_2_out;

  Clock clock_1 (.out(clock_1_out));
  Shift_Register #(.length(4)) shift_register_1 (
    .shift(Shift_Enable), .in(Serial_Input), .clk(clock_1_out), .out(shift_register_1_out));  // open: load, clr, d0, q0, d1, q1, d2, q2, d3, q3
  Shift_Register #(.length(4)) shift_register_2 (
    .shift(Shift_Enable), .in(Serial_Input), .clk(clock_1_out), .out(shift_register_2_out));  // open: load, clr, d0, q0, d1, q1, d2, q2, d3, q3
  Adder #(.width(1)) adder_1 (
    .a(shift_register_1_out), .b(shift_register_2_out), .out(adder_1_out), .cin(d_ff_1_q), .cout(out_3));
  D_Flip_Flop d_ff_1 (.clk(clock_1_out), .D(out_3), .Q(d_ff_1_q));  // open: Qn, preset, en, reset
  Shift_Register #(.length(4)) shift_register_3 (
    .shift(Shift_Enable), .in(adder_1_out), .clk(clock_1_out));  // open: out, load, clr, d0, q0, d1, q1, d2, q2, d3, q3

  // Notes on the sheet:
  //   Clock
endmodule
